# Fritzing sketch CircuitTimeMap (saved by Fritzing 0.9.3b)
breadboards: 1

parts:
  Part1 = Arduino Uno (Rev3)
  ZS-042_RTC1 = ZS-042 RTC Module
  RGB_SMD_LED1 = SMD RGB LED (WS2812) [package=5050]
  RGB_SMD_LED2 = SMD RGB LED (WS2812) [package=5050]

nets:
  N1: Part1.A4/SDA, ZS-042_RTC1.SDA
  N2: Part1.A5/SCL, ZS-042_RTC1.SCL
  N3: Part1.D5_PWM, RGB_SMD_LED2.DIn
  N4: Part1.D6_PWM, RGB_SMD_LED1.DIn
  VCC: Part1.5V, ZS-042_RTC1.VCC, RGB_SMD_LED1.VCC, RGB_SMD_LED2.VCC
  GND: Part1.GND, ZS-042_RTC1.GND, RGB_SMD_LED1.VSS, RGB_SMD_LED2.VSS
